# Fritzing sketch Opto-Isolator (saved by Fritzing 0.9.2b)
circuit board: 8.46667cm x 5.64444cm
breadboards: 1

parts:
  R1 = Resistor [tolerance=±5% resistance=3.3k package=THT]
  J1 = female pin header, 2 pins [form="♀ (female)"]
  C2 = Ceramic Capacitor [capacitance=100nF package="100 mil [THT, multilayer]"]
  J2 = female pin header, 2 pins [form="♀ (female)"]
  D1 = Schottky Diode [part_number=1N5818 package="300 mil [THT]"]
  C1 = Ceramic Capacitor [capacitance=0.1nF voltage=35V package="100 mil [THT, multilayer]"]
  R3 = Resistor [tolerance=±5% resistance=1k package=THT]
  IC1 = 6n137 Optocoupler [chip_label=6n137 package="DIP (Dual Inline) [THT]"]
  R2 = Resistor [tolerance=±5% resistance=3.3k package=THT]

nets (from the schematic view):
  N1: R1.Pin_0, J1.pin1, R2.Pin_0
  N2: R1.Pin_1, D1.cathode, C1.1, IC1.Vf+, R2.Pin_1
  N3: J1.pin2, D1.anode, C1.0, IC1.Vf-
  GND: C2.0, J2.pin2, IC1.GND
  5V: C2.1, R3.Pin_0, IC1.Vcc
  N4: J2.pin1, R3.Pin_1, IC1.Vo

notes:
  Opto-isolator Circuit
  Fairchild 6n137 fast opto-coupler, 10Mbits/s rated
  Reverse protection diode is shottky with 30V or higher rating (1N5818 is 30V peak, 1A part)
  Input capacitor C1 should be 30V rated or higher
  Input LED forward voltage ~1.4V typ at 10mA forward current
  1MHz noise cutoff using input RC Low Pass filter, with 0.4us rise time
  Input current limit resistor is two 0.25W 3.3k resistors in parallel
  1.65k delivers
  ~9mA from 15V,
  ~15mA max at rated input voltage
  ~3.7mA at low input of 7V
  max power 300mW in input resistors at max voltage
  Larger input resistor can be used at expense of raising low end input voltage limit for reliable operation
  High level output current max 20uA results in 20mV offset
  Input threshold approx 2.5mA with 1k load resistor
  Designed for inputs of between 7V and 24V, 12-15V nominal
  Ve is for strobing the output and can be left NC if not used as has internal pullup
  Output resistor allows for full output low voltage at >5mA output current
  0.1uF Vcc decoupling required close to Vcc and GND pins
  For connection to Raspberry Pi use a level converter to convert from 5V logic to 3.3V.
  Input 7V to 24V, 15V nominal, 500kHz
  Note that grounds are not joined between source and circuit.
  Example use:
  DCC decoder front end isolator feeding Arduino
  This work by hobbyistdave is licensed under a Creative Commons Attribution-ShareAlike 4.0 International License
  No warranty either express or implied is given.
  This schematic was created with Fritzing.
  Inspired by Geoff Bunza at
  http://model-railroad-hobbyist.com/node/19446

custom parts:
  6n137 Optocoupler: 6n137 fast Optocoupler. With 8 pins on a 300mil dual inline package (DIP) footprint. Ve is strobe input. Output is inverting.
