# Fritzing sketch breadboard_0 (saved by Fritzing 0.9.6b)
breadboards: 3

parts:
  U1 = MIDI_CONN_FEMALE [package=din_5_female]
  RE2 = Rotary Encoder [package=THT]
  Part1 = Adafruit MCP4725 Breakout Board - 12-Bit DAC [part_number="Adafruit #935"]
  S7 = Momentary Switch [package=ksa_sealed_tac_switch]
  S8 = Momentary Switch [package=ksa_sealed_tac_switch]
  D1 = LTE-302 [package=lte-302]
  U2 = LM358 [package=dip08]
  D2 = Rectifier Diode [part_number=1N4001 package="Melf DO-213 AB [SMD]"]
  IC1 = IC, DIP package, 8 pins [chip_label=6N138]
  R9 = Resistor [tolerance=±5% resistance=220 power=0.25 package=THT]
  R10 = Resistor [tolerance=±5% resistance=220 package="2010 [SMD]"]
  R11 = Resistor [tolerance=±5% resistance=220 package="0603 [SMD]"]
  R12 = Resistor [tolerance=±5% resistance=2.2k package="2512 [SMD]"]
  R13 = Resistor [tolerance=±5% resistance=4.7k package="2512 [SMD]"]
  R14 = Resistor [tolerance=±5% resistance=100 package="2512 [SMD]"]
  R15 = Resistor [tolerance=±5% resistance=10k package="2512 [SMD]"]
  C5 = Capacitor [package=cap-pth-small2]
  C6 = Capacitor [package=cap-pth-small2]
  R16 = Resistor [tolerance=±5% resistance=10k package="2512 [SMD]"]
  R17 = Resistor [tolerance=±5% resistance=10k package="2512 [SMD]"]
  D3 = LTE-302 [package=lte-302]
  R18 = Resistor [tolerance=±5% resistance=220 package="0603 [SMD]"]
  R19 = Resistor [tolerance=±5% resistance=10k package="2512 [SMD]"]
  R20 = Resistor [tolerance=±5% resistance=10k package="2512 [SMD]"]
  R21 = Resistor [tolerance=±5% resistance=10k package="2512 [SMD]"]
  C8 = Capacitor [package=cap-pth-small2]
  JP3 = Header 1 [package=1x01_offset]
  JP4 = Header 1 [package=1x01_offset]
  Part2 = Adafruit MicroSD card breakout board [part_number="Adafruit #254"]
  R22 = Resistor [tolerance=±5% resistance=10k package="2512 [SMD]"]  # not connected
  Part3 = Adafruit MCP4725 Breakout Board - 12-Bit DAC [part_number="Adafruit #935"]
  TRRS1 = Audio Jack (TRRS) 3.5mm [part_number="LUMBERG JEITA RC-5325A" package="RC-5325A [SMD]"]  # not connected
  TRRS2 = Audio Jack (TRRS) 3.5mm [part_number="LUMBERG JEITA RC-5325A" package="RC-5325A [SMD]"]  # not connected
  TRRS3 = Audio Jack (TRRS) 3.5mm [part_number="LUMBERG JEITA RC-5325A" package="RC-5325A [SMD]"]  # not connected
  TRRS4 = Audio Jack (TRRS) 3.5mm [part_number="LUMBERG JEITA RC-5325A" package="RC-5325A [SMD]"]  # not connected
  U3 = LM358 [package=dip08]
  R23 = Resistor [tolerance=±5% resistance=100 package="2512 [SMD]"]
  R24 = Resistor [tolerance=±5% resistance=10k package="2512 [SMD]"]
  C9 = Capacitor [package=cap-pth-small2]
  Mod1 = Raspberry Pi Pico

nets:
  GND: U1.NC1, Part1.GND, S7.3, S7.4, S8.3, S8.4, D1.C, U2.G$1_V-, IC1.pin5, R12.Pin_1, C5.2, C6.1, D3.C, C8.2, JP4.1, Part2.GND, Part3.GND, U3.G$1_V-, C9.2, Mod1.pin_3, Mod1.pin_8, Mod1.pin_13, Mod1.pin_18, Mod1.pin_23, Mod1.pin_28, Mod1.pin_33, Mod1.pin_38
  N1: U1.MIDI_IN, D2.anode, IC1.pin3
  N2: U1.MIDI_OUT, R10.Pin_0
  N3: RE2.EncoderPinA, R21.Pin_1
  N4: RE2.EncoderPinB, R20.Pin_0
  N5: RE2.SwitchrPinD, R23.Pin_1
  VDD: Part1.VDD, Part3.VDD, Mod1.pin_39
  N6: Part1.SCL, Part3.SCL, Mod1.pin_22
  N7: Part1.SDA, Part3.SDA, Mod1.pin_21
  N8: Part1.VOUT, U2.G$1_+IN
  N9: S7.1, S7.2, R14.Pin_1
  N10: S8.1, S8.2, Mod1.pin_30
  N11: D1.A, R11.Pin_0
  N12: U2.G$1_OUT, R13.Pin_0
  N13: U2.G$1_-IN, R12.Pin_0, R13.Pin_1
  N14: U2.G$2_-IN, U2.G$2_OUT
  N15: D2.cathode, IC1.pin2, R10.Pin_1
  N16: IC1.pin6, R9.Pin_1, Mod1.pin_7
  N17: IC1.pin8, R9.Pin_0
  N18: R11.Pin_1, Mod1.pin_4
  N19: R14.Pin_0, R15.Pin_1, C5.1, Mod1.pin_9
  N20: R15.Pin_0, R16.Pin_0, R19.Pin_0, U3.G$1_V+
  N21: C6.2, R16.Pin_1, R21.Pin_0, Mod1.pin_2
  N22: R17.Pin_1, R23.Pin_0, R24.Pin_0, C9.1
  N23: D3.A, R18.Pin_1
  N24: R19.Pin_1, R20.Pin_1, C8.1, Mod1.pin_1
  N25: JP3.1, Mod1.pin_40
  N26: Part2.+3V3, Mod1.pin_36
  N27: Part2.CD, Mod1.pin_29
  GND_2: Mod1.pin_20

notes:
  +5V
  +3V
  Reset
  DC - DC Step Up
  Midi In
  SD Card
  OLED I2C Display
  12 bit DAC MPC 4725
  Raspberry Pico Pi
  16 bit DAC Pico Audio Shield
  Startup LED
  Rotary Encoder
  Switch Edit Mode
  Midi LED
  Power in 5V
  USB
  CV Out 0-10V
  Gate/Trigger Out 5V

custom parts:
  Rotary Encoder: Rotary Encoder from ALPSec11e with switch.
  Adafruit MCP4725 Breakout Board - 12-Bit DAC: Your microcontroller probably has an ADC (analog -> digital converter) but does it have a DAC (digital -> analog converter)??? Now it can! This breakout board features the easy-to-use MCP4725 12-bit DAC. Control it via I2C and send it the value you want it to output, and the VOUT pin will have it. Great for audio / analog projects, such as when you can't use PWM but need a sine wave or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
  Adafruit MicroSD card breakout board: Not just a simple breakout board, this microSD adapter goes the extra mile - designed for ease of use. Onboard 5v->3v regulator provides 150mA for power-hungry cards 3v level shifting means you can use this with ease on either 3v or 5v systems Uses a proper level shifting chip, not resistors: less problems, and faster read/write access Use 3 or 4 digital pins to read and write 2Gb+ of storage!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
  Raspberry Pi Pico: Raspberry Pi Pico. Based around the RP2040 microcontroller the Pico is a low cost microcontroller device bringing Raspberry Pi quality, cost, and easy of use to the microcontroller space. Jan 2021, Split part in to two versions: tht (this one) and SMD. This one will drill holes for a .1 in header in pcb to allow plugging in the module as well as providing pads to solder the module to the top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
