# Fritzing sketch breadboard_0 (saved by Fritzing 0.9.6b)
breadboards: 2

parts:
  Mod1 = Raspberry Pi Pico
  U1 = MIDI_CONN_FEMALE [package=din_5_female]
  RE2 = Rotary Encoder [package=THT]
  Part1 = Adafruit MCP4725 Breakout Board - 12-Bit DAC [part_number="Adafruit #935"]
  S7 = Momentary Switch [package=ksa_sealed_tac_switch]
  S8 = Momentary Switch [package=ksa_sealed_tac_switch]
  D1 = LTE-302 [package=lte-302]
  microSD1 = MicroSD Card Module  # not connected
  U2 = LM358 [package=dip08]
  D2 = Rectifier Diode [part_number=1N4001 package="Melf DO-213 AB [SMD]"]
  JP1 = Header 1 [package=1x01_offset]
  JP2 = Header 1 [package=1x01_offset]  # not connected
  R6 = Resistor [tolerance=±5% power=0.25 resistance=10k package=THT]
  IC1 = IC, DIP package, 8 pins [chip_label=6N138]
  R7 = Resistor [tolerance=±5% resistance=220 package="0402 [SMD]"]  # not connected
  R8 = Resistor [tolerance=±5% resistance=220 package="0402 [SMD]"]
  R9 = Resistor [tolerance=±5% resistance=220 power=0.25 package=THT]
  R10 = Resistor [tolerance=±5% resistance=220 package="2010 [SMD]"]
  R11 = Resistor [tolerance=±5% resistance=220 package="0603 [SMD]"]
  R12 = Resistor [tolerance=±5% resistance=2.2k package="2512 [SMD]"]
  R13 = Resistor [tolerance=±5% resistance=4.7k package="2512 [SMD]"]
  R14 = Resistor [tolerance=±5% resistance=100 package="2512 [SMD]"]
  R15 = Resistor [tolerance=±5% resistance=10k package="2512 [SMD]"]
  C5 = Capacitor [package=cap-pth-small2]
  C6 = Capacitor [package=cap-pth-small2]
  R16 = Resistor [tolerance=±5% resistance=10k package="2512 [SMD]"]
  R17 = Resistor [tolerance=±5% resistance=10k package="2512 [SMD]"]
  D3 = LTE-302 [package=lte-302]
  R18 = Resistor [tolerance=±5% resistance=220 package="0603 [SMD]"]
  R19 = Resistor [tolerance=±5% resistance=10k package="2512 [SMD]"]
  R20 = Resistor [tolerance=±5% resistance=10k package="2512 [SMD]"]
  R21 = Resistor [tolerance=±5% resistance=10k package="2512 [SMD]"]
  C7 = Capacitor [package=cap-pth-small2]
  C8 = Capacitor [package=cap-pth-small2]
  JP3 = Header 1 [package=1x01_offset]
  JP4 = Header 1 [package=1x01_offset]

nets:
  N1: Mod1.pin_1, R6.Pin_1, R21.Pin_1, C8.2
  N2: Mod1.pin_2, R20.Pin_1, C7.2
  N3: Mod1.pin_3, Mod1.pin_8, Mod1.pin_13, Mod1.pin_18, Mod1.pin_23, Mod1.pin_28, Mod1.pin_33, Mod1.pin_38, Mod1.pin_42, U1.NC1, Part1.GND, S8.2, S8.4, D1.C, U2.G$1_V-, JP1.1, IC1.pin5, R8.Pin_1, R12.Pin_1, R14.Pin_1, C5.2, C6.1, D3.C, C8.1, JP3.1
  N4: Mod1.pin_4, R11.Pin_1
  N5: Mod1.pin_7, C6.2, R17.Pin_1
  N6: Mod1.pin_9, S7.4, R15.Pin_1
  N7: Mod1.pin_10, S8.1, S8.3
  N8: Mod1.pin_14, R18.Pin_0
  GND: Mod1.pin_20
  N9: Mod1.pin_21, Part1.SDA
  N10: Mod1.pin_22, Part1.SCL
  N11: Mod1.pin_27, IC1.pin6, R9.Pin_1
  N12: Mod1.pin_36, IC1.pin8, R9.Pin_0
  N13: Mod1.pin_40, JP4.1
  N14: U1.NC2, D2.anode, IC1.pin3
  N15: U1.MIDI_OUT, R10.Pin_0
  N16: RE2.EncoderPinA, R16.Pin_1, R21.Pin_0
  N17: RE2.EncoderPinC, U2.G$2_+IN, C7.1
  N18: RE2.EncoderPinB, R19.Pin_1, R20.Pin_0
  N19: RE2.SwitchPinE, R8.Pin_0
  N20: Part1.VOUT, U2.G$1_+IN
  N21: S7.1, R14.Pin_0
  N22: S7.3, C5.1
  N23: D1.A, R11.Pin_0
  N24: U2.G$1_OUT, R13.Pin_0
  N25: U2.G$1_-IN, R12.Pin_0, R13.Pin_1
  N26: U2.G$2_-IN, U2.G$2_OUT
  N27: D2.cathode, IC1.pin2, R10.Pin_1
  N28: R15.Pin_0, R17.Pin_0, R19.Pin_0
  N29: D3.A, R18.Pin_1

notes:
  +5V
  +3V
  Reset
  CV Out 0-10V
  DC - DC Step Up
  Midi In
  SD Card
  OLED I2C Display
  12 bit DAC MPC 4725
  Raspberry Pico Pi
  16 bit DAC Pico Audio Shield
  Startup LED
  Rotary Encoder
  Switch Edit Mode
  Midi LED
  Power in 5V
  USB

custom parts:
  Raspberry Pi Pico: Raspberry Pi Pico. Based around the RP2040 microcontroller the Pico is a low cost microcontroller device bringing Raspberry Pi quality, cost, and easy of use to the microcontroller space. Jan 2021, Split part in to two versions: tht (this one) and SMD. This one will drill holes for a .1 in header in pcb to allow plugging in the module as well as providing pads to solder the module to the top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
  Rotary Encoder: Rotary Encoder from ALPSec11e with switch.
  Adafruit MCP4725 Breakout Board - 12-Bit DAC: Your microcontroller probably has an ADC (analog -> digital converter) but does it have a DAC (digital -> analog converter)??? Now it can! This breakout board features the easy-to-use MCP4725 12-bit DAC. Control it via I2C and send it the value you want it to output, and the VOUT pin will have it. Great for audio / analog projects, such as when you can't use PWM but need a sine wave or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
